// Logisim project ALU.circ as structural Verilog: 5 circuits, main circuit ALU One Bit
// FAOB
module Full_Adder_One_Bit (
  input  B1,
  input  C1,
  input  CIN,
  input  OP,
  output R,
  output COUT
);

  wire and_1_out, and_2_out, and_3_out, and_4_out, and_5_out, and_6_out, and_7_out, and_8_out, and_9_out,
       not_1_out, not_2_out, not_3_out, not_4_out, not_5_out, not_6_out, not_7_out, not_8_out, not_9_out,
       not_10_out;

  not not_1 (not_1_out, B1);
  not not_2 (not_2_out, C1);
  and and_1 (and_1_out, not_1_out, not_2_out, CIN);
  not not_3 (not_3_out, B1);
  and and_2 (and_2_out, not_3_out, C1, not_4_out);
  not not_4 (not_4_out, CIN);
  and and_3 (and_3_out, B1, not_5_out, not_6_out);
  not not_5 (not_5_out, C1);
  not not_6 (not_6_out, CIN);
  and and_4 (and_4_out, B1, C1, CIN, OP);
  not not_7 (not_7_out, B1);
  and and_5 (and_5_out, not_7_out, CIN, not_8_out);
  not not_8 (not_8_out, OP);
  not not_9 (not_9_out, B1);
  and and_6 (and_6_out, not_9_out, C1, not_10_out);
  not not_10 (not_10_out, OP);
  and and_7 (and_7_out, C1, CIN);
  and and_8 (and_8_out, B1, CIN, OP);
  and and_9 (and_9_out, B1, C1, OP);
  or or_1 (R, and_1_out, and_2_out, and_3_out, and_4_out);
  or or_2 (COUT, and_5_out, and_6_out, and_7_out, and_8_out, and_9_out);
endmodule

// ZL
module Zero_Logic (
  input  RESULT,
  input  CIN,
  input  SUB,
  output ZERO
);

  wire not_1_out, not_2_out;

  not not_1 (not_1_out, RESULT);
  not not_2 (not_2_out, CIN);
  and and_1 (ZERO, not_1_out, not_2_out, SUB);
endmodule

// ALUOB
module ALU_One_Bit (
  input  R1,
  input  R2,
  input  CIN,
  input  [2:0] ALU_CODE,
  output ZERO,
  output COUT,
  output RESULT
);

  wire and_1_out, and_2_out, full_adder_one_bit_1_r, not_1_out, not_2_out, or_1_out;

  Full_Adder_One_Bit full_adder_one_bit_1 (
    .B1(R1), .C1(R2), .CIN(CIN), .R(full_adder_one_bit_1_r), .OP(ALU_CODE[2]), .COUT(COUT));
  not not_1 (not_1_out, ALU_CODE[2]);
  and and_1 (and_1_out, not_1_out, ALU_CODE[0]);
  or or_1 (or_1_out, R1, R2);
  and and_2 (and_2_out, R1, R2);
  not not_2 (not_2_out, or_1_out);
  Multiplexer #(.select(3)) multiplexer_1 (
    .in0(COUT), .in1(full_adder_one_bit_1_r), .in4(full_adder_one_bit_1_r), .in5(not_2_out), .in6(and_2_out),
    .in7(or_1_out), .out(RESULT), .sel(ALU_CODE));  // open: in2, in3, en
  Zero_Logic zero_logic_1 (.RESULT(full_adder_one_bit_1_r), .CIN(COUT), .SUB(and_1_out), .ZERO(ZERO));
endmodule

// ALUEB
module ALU_Eight_Bits (
  input  [2:0] ALU_CODE,
  input  [7:0] R2,
  input  CIN,
  input  [7:0] R1,
  output [7:0] RESULT,
  output COUT,
  output ZERO
);

  wire _0_cout, _0_zero, _1_cout, _1_zero, _2_cout, _2_zero, _3_cout, _3_zero, _4_cout, _4_zero, _5_cout,
       _5_zero, _6_cout, _6_zero, _7_zero, not_1_out, R0, R1_t, R2_t, R3, R4, R5, R6, R7;
  wire [7:7] and_1_out;

  Multiplexer #(.select(3), .width(8)) multiplexer_1 (
    .in0({{7{and_1_out[7]}}, R7}), .in1({R7, R6, R5, R4, R3, R2_t, R1_t, R0}),
    .in4({R7, R6, R5, R4, R3, R2_t, R1_t, R0}), .in5({R7, R6, R5, R4, R3, R2_t, R1_t, R0}),
    .in6({R7, R6, R5, R4, R3, R2_t, R1_t, R0}), .in7({R7, R6, R5, R4, R3, R2_t, R1_t, R0}), .out(RESULT),
    .sel(ALU_CODE));  // open: in2, in3, en
  and and_1 (and_1_out[7], R7, not_1_out);
  not not_1 (not_1_out, R7);
  ALU_One_Bit _7 (.R1(R1[7]), .R2(R2[7]), .CIN(_6_cout), .ALU_CODE(ALU_CODE), .ZERO(_7_zero), .COUT(COUT), .RESULT(R7));
  ALU_One_Bit _6 (
    .R1(R1[6]), .R2(R2[6]), .CIN(_5_cout), .ALU_CODE(ALU_CODE), .ZERO(_6_zero), .COUT(_6_cout), .RESULT(R6));
  ALU_One_Bit _4 (
    .R1(R1[4]), .R2(R2[4]), .CIN(_3_cout), .ALU_CODE(ALU_CODE), .ZERO(_4_zero), .COUT(_4_cout), .RESULT(R4));
  ALU_One_Bit _5 (
    .R1(R1[5]), .R2(R2[5]), .CIN(_4_cout), .ALU_CODE(ALU_CODE), .ZERO(_5_zero), .COUT(_5_cout), .RESULT(R5));
  ALU_One_Bit _3 (
    .R1(R1[3]), .R2(R2[3]), .CIN(_2_cout), .ALU_CODE(ALU_CODE), .ZERO(_3_zero), .COUT(_3_cout), .RESULT(R3));
  ALU_One_Bit _2 (
    .R1(R1[2]), .R2(R2[2]), .CIN(_1_cout), .ALU_CODE(ALU_CODE), .ZERO(_2_zero), .COUT(_2_cout), .RESULT(R2_t));
  ALU_One_Bit _1 (
    .R1(R1[1]), .R2(R2[1]), .CIN(_0_cout), .ALU_CODE(ALU_CODE), .ZERO(_1_zero), .COUT(_1_cout), .RESULT(R1_t));
  and and_2 (ZERO, _7_zero, _6_zero, _5_zero, _4_zero, _3_zero, _2_zero, _1_zero, _0_zero);
  ALU_One_Bit _0 (.R1(R1[0]), .R2(R2[0]), .CIN(CIN), .ALU_CODE(ALU_CODE), .ZERO(_0_zero), .COUT(_0_cout), .RESULT(R0));
endmodule

// ALUTTB
module ALU_Thirty_Two_Bits (
  input  [2:0] ALU_CODE,
  input  [31:0] R2,
  input  CIN,
  input  [31:0] R1,
  output [31:0] RESULT,
  output ZERO
);

  wire _0_cout, _0_zero, _1_cout, _1_zero, _2_cout, _2_zero, _3_zero;
  wire [7:0] not_1_out;
  wire [31:0] _0_result;
  wire [31:24] and_1_out;

  Multiplexer #(.select(3), .width(32)) multiplexer_1 (
    .in0({and_1_out, and_1_out, and_1_out, _0_result[31:24]}), .in1(_0_result), .in4(_0_result),
    .in5(_0_result), .in6(_0_result), .in7(_0_result), .out(RESULT), .sel(ALU_CODE));  // open: in2, in3, en
  assign and_1_out = _0_result[31:24] & not_1_out;  // AND_Gate and_1, 8 bits wide
  assign not_1_out = ~_0_result[31:24];  // NOT_Gate not_1, 8 bits wide
  ALU_Eight_Bits _3 (
    .ALU_CODE(ALU_CODE), .RESULT(_0_result[31:24]), .R2(R2[31:24]), .CIN(_2_cout), .R1(R1[31:24]),
    .ZERO(_3_zero));  // open: COUT
  ALU_Eight_Bits _2 (
    .ALU_CODE(ALU_CODE), .COUT(_2_cout), .RESULT(_0_result[23:16]), .R2(R2[23:16]), .CIN(_1_cout),
    .R1(R1[23:16]), .ZERO(_2_zero));
  ALU_Eight_Bits _1 (
    .ALU_CODE(ALU_CODE), .COUT(_1_cout), .RESULT(_0_result[15:8]), .R2(R2[15:8]), .CIN(_0_cout),
    .R1(R1[15:8]), .ZERO(_1_zero));
  ALU_Eight_Bits _0 (
    .ALU_CODE(ALU_CODE), .COUT(_0_cout), .RESULT(_0_result[7:0]), .R2(R2[7:0]), .CIN(CIN), .R1(R1[7:0]),
    .ZERO(_0_zero));
  and and_2 (ZERO, _3_zero, _2_zero, _1_zero, _0_zero);
endmodule
