// Logisim project Fundamental MEM REG Components.circ as structural Verilog: 7 circuits, main circuit Normal Eight Register
// ZER
module Zero_Eight_Register (
  input  [31:0] WD,
  input  CLK,
  input  [2:0] WR,
  input  ENWR,
  input  [2:0] R1,
  input  [2:0] R2,
  input  ENR1,
  input  ENR2,
  output [31:0] R1_2,
  output [31:0] R2_2
);

  wire and_1_out, and_2_out, and_3_out, and_4_out, and_5_out, and_6_out, and_7_out, decoder_1_out1,
       decoder_1_out2, decoder_1_out3, decoder_1_out4, decoder_1_out5, decoder_1_out6, decoder_1_out7;
  wire [31:0] _0_q, _1_q, _2_q, _3_q, _4_q, _5_q, _6_q, _7_q;

  Decoder #(.select(3)) decoder_1 (
    .out1(decoder_1_out1), .out2(decoder_1_out2), .out3(decoder_1_out3), .out4(decoder_1_out4),
    .out5(decoder_1_out5), .out6(decoder_1_out6), .out7(decoder_1_out7), .sel(WR));  // open: out0, en
  Register #(.width(32)) _0 (.Q(_0_q));  // open: D, en, clk, clr
  and and_1 (and_1_out, decoder_1_out1, ENWR);
  Multiplexer #(.select(3), .width(32)) multiplexer_1 (
    .in0(_0_q), .in1(_1_q), .in2(_2_q), .in3(_3_q), .in4(_4_q), .in5(_5_q), .in6(_6_q), .in7(_7_q),
    .out(R1_2), .sel(R1), .en(ENR1));
  Register #(.width(32)) _1 (.D(WD), .en(and_1_out), .Q(_1_q), .clk(CLK));  // open: clr
  and and_2 (and_2_out, decoder_1_out2, ENWR);
  Register #(.width(32)) _2 (.D(WD), .en(and_2_out), .Q(_2_q), .clk(CLK));  // open: clr
  and and_3 (and_3_out, decoder_1_out3, ENWR);
  Register #(.width(32)) _3 (.D(WD), .en(and_3_out), .Q(_3_q), .clk(CLK));  // open: clr
  and and_4 (and_4_out, decoder_1_out4, ENWR);
  Multiplexer #(.select(3), .width(32)) multiplexer_2 (
    .in0(_0_q), .in1(_1_q), .in2(_2_q), .in3(_3_q), .in4(_4_q), .in5(_5_q), .in6(_6_q), .in7(_7_q),
    .out(R2_2), .sel(R2), .en(ENR2));
  Register #(.width(32)) _4 (.D(WD), .en(and_4_out), .Q(_4_q), .clk(CLK));  // open: clr
  and and_5 (and_5_out, decoder_1_out5, ENWR);
  Register #(.width(32)) _5 (.D(WD), .en(and_5_out), .Q(_5_q), .clk(CLK));  // open: clr
  and and_6 (and_6_out, decoder_1_out6, ENWR);
  Register #(.width(32)) _6 (.D(WD), .en(and_6_out), .Q(_6_q), .clk(CLK));  // open: clr
  and and_7 (and_7_out, decoder_1_out7, ENWR);
  Register #(.width(32)) _7 (.D(WD), .en(and_7_out), .Q(_7_q), .clk(CLK));  // open: clr
endmodule

// NER
module Normal_Eight_Register (
  input  [31:0] WD,
  input  CLK,
  input  [2:0] WR,
  input  ENWR,
  input  [2:0] R1,
  input  [2:0] R2,
  input  ENR1,
  input  ENR2,
  output [31:0] R1_2,
  output [31:0] R2_2
);

  wire and_1_out, and_2_out, and_3_out, and_4_out, and_5_out, and_6_out, and_7_out, and_8_out,
       decoder_1_out0, decoder_1_out1, decoder_1_out2, decoder_1_out3, decoder_1_out4, decoder_1_out5,
       decoder_1_out6, decoder_1_out7;
  wire [31:0] _0_q, _1_q, _2_q, _3_q, _4_q, _5_q, _6_q, _7_q;

  Decoder #(.select(3)) decoder_1 (
    .out0(decoder_1_out0), .out1(decoder_1_out1), .out2(decoder_1_out2), .out3(decoder_1_out3),
    .out4(decoder_1_out4), .out5(decoder_1_out5), .out6(decoder_1_out6), .out7(decoder_1_out7), .sel(WR));  // open: en
  and and_1 (and_1_out, decoder_1_out0, ENWR);
  Register #(.width(32)) _0 (.D(WD), .en(and_1_out), .Q(_0_q), .clk(CLK));  // open: clr
  and and_2 (and_2_out, decoder_1_out1, ENWR);
  Multiplexer #(.select(3), .width(32)) multiplexer_1 (
    .in0(_0_q), .in1(_1_q), .in2(_2_q), .in3(_3_q), .in4(_4_q), .in5(_5_q), .in6(_6_q), .in7(_7_q),
    .out(R1_2), .sel(R1), .en(ENR1));
  Register #(.width(32)) _1 (.D(WD), .en(and_2_out), .Q(_1_q), .clk(CLK));  // open: clr
  and and_3 (and_3_out, decoder_1_out2, ENWR);
  Register #(.width(32)) _2 (.D(WD), .en(and_3_out), .Q(_2_q), .clk(CLK));  // open: clr
  and and_4 (and_4_out, decoder_1_out3, ENWR);
  Register #(.width(32)) _3 (.D(WD), .en(and_4_out), .Q(_3_q), .clk(CLK));  // open: clr
  and and_5 (and_5_out, decoder_1_out4, ENWR);
  Multiplexer #(.select(3), .width(32)) multiplexer_2 (
    .in0(_0_q), .in1(_1_q), .in2(_2_q), .in3(_3_q), .in4(_4_q), .in5(_5_q), .in6(_6_q), .in7(_7_q),
    .out(R2_2), .sel(R2), .en(ENR2));
  Register #(.width(32)) _4 (.D(WD), .en(and_5_out), .Q(_4_q), .clk(CLK));  // open: clr
  and and_6 (and_6_out, decoder_1_out5, ENWR);
  Register #(.width(32)) _5 (.D(WD), .en(and_6_out), .Q(_5_q), .clk(CLK));  // open: clr
  and and_7 (and_7_out, decoder_1_out6, ENWR);
  Register #(.width(32)) _6 (.D(WD), .en(and_7_out), .Q(_6_q), .clk(CLK));  // open: clr
  and and_8 (and_8_out, decoder_1_out7, ENWR);
  Register #(.width(32)) _7 (.D(WD), .en(and_8_out), .Q(_7_q), .clk(CLK));  // open: clr
endmodule

// SPER
module SP_Eight_Register (
  input  [31:0] WD,
  input  CLK,
  input  [2:0] WR,
  input  ENWR,
  input  [2:0] R1,
  input  [2:0] R2,
  input  ENR1,
  input  ENR2,
  output [31:0] R1_2,
  output [31:0] R2_2
);

  wire and_1_out, and_2_out, and_3_out, and_4_out, and_5_out, and_6_out, and_7_out, and_8_out,
       decoder_1_out0, decoder_1_out1, decoder_1_out2, decoder_1_out3, decoder_1_out4, decoder_1_out5,
       decoder_1_out6, decoder_1_out7;
  wire [31:0] _0_q, _1_q, _2_q, _3_q, _4_q, _5_q, _6_q, _7_q;

  Decoder #(.select(3)) decoder_1 (
    .out0(decoder_1_out0), .out1(decoder_1_out1), .out2(decoder_1_out2), .out3(decoder_1_out3),
    .out4(decoder_1_out4), .out5(decoder_1_out5), .out6(decoder_1_out6), .out7(decoder_1_out7), .sel(WR));  // open: en
  and and_1 (and_1_out, decoder_1_out0, ENWR);
  Register #(.width(32)) _0 (.D(WD), .en(and_1_out), .Q(_0_q), .clk(CLK));  // open: clr
  and and_2 (and_2_out, decoder_1_out1, ENWR);
  Multiplexer #(.select(3), .width(32)) multiplexer_1 (
    .in0(_0_q), .in1(_1_q), .in2(_2_q), .in3(_3_q), .in4(_4_q), .in5(_5_q), .in6(_6_q), .in7(_7_q),
    .out(R1_2), .sel(R1), .en(ENR1));
  Register #(.width(32)) _1 (.D(WD), .en(and_2_out), .Q(_1_q), .clk(CLK));  // open: clr
  and and_3 (and_3_out, decoder_1_out2, ENWR);
  Register #(.width(32)) _2 (.D(WD), .en(and_3_out), .Q(_2_q), .clk(CLK));  // open: clr
  and and_4 (and_4_out, decoder_1_out3, ENWR);
  Register #(.width(32)) _3 (.D(WD), .en(and_4_out), .Q(_3_q), .clk(CLK));  // open: clr
  and and_5 (and_5_out, decoder_1_out4, ENWR);
  Multiplexer #(.select(3), .width(32)) multiplexer_2 (
    .in0(_0_q), .in1(_1_q), .in2(_2_q), .in3(_3_q), .in4(_4_q), .in5(_5_q), .in6(_6_q), .in7(_7_q),
    .out(R2_2), .sel(R2), .en(ENR2));
  Register #(.width(32)) _4 (.D(WD), .en(and_5_out), .Q(_4_q), .clk(CLK));  // open: clr
  and and_6 (and_6_out, decoder_1_out5, ENWR);
  Register #(.width(32)) _5 (.D(WD), .en(and_6_out), .Q(_5_q), .clk(CLK));  // open: clr
  and and_7 (and_7_out, decoder_1_out6, ENWR);
  Register #(.width(32)) _6 (.D(WD), .en(and_7_out), .Q(_6_q), .clk(CLK));  // open: clr
  and and_8 (and_8_out, decoder_1_out7, ENWR);
  Register #(.width(32)) _7 (.D(WD), .en(and_8_out), .Q(_7_q), .clk(CLK));  // open: clr
endmodule

// RB
module Register_Bank (
  input  Clk,
  input  [4:0] R1,
  input  [4:0] R2,
  input  [4:0] WR,
  input  ENWR,
  input  [31:0] WD,
  output [31:0] R1_2,
  output [31:0] R2_2
);

  wire decoder_1_out0, decoder_1_out1, decoder_1_out2, decoder_1_out3, decoder_2_out0, decoder_2_out1,
       decoder_2_out2, decoder_2_out3, decoder_3_out0, decoder_3_out1, decoder_3_out2, decoder_3_out3,
       not_1_out;

  Decoder #(.select(2)) decoder_1 (
    .out0(decoder_1_out0), .out1(decoder_1_out1), .out2(decoder_1_out2), .out3(decoder_1_out3), .sel(R1[4:3]));  // open: en
  Decoder #(.select(2)) decoder_2 (
    .out0(decoder_2_out0), .out1(decoder_2_out1), .out2(decoder_2_out2), .out3(decoder_2_out3), .sel(R2[4:3]));  // open: en
  Decoder #(.select(2)) decoder_3 (
    .out0(decoder_3_out0), .out1(decoder_3_out1), .out2(decoder_3_out2), .out3(decoder_3_out3),
    .sel(WR[4:3]), .en(ENWR));
  assign decoder_3_out3 = not_1_out ? ENWR : 1'bz;  // Controlled_Buffer controlled_buffer_1
  assign decoder_3_out2 = not_1_out ? ENWR : 1'bz;  // Controlled_Buffer controlled_buffer_2
  not not_1 (not_1_out, ENWR);
  assign decoder_3_out1 = not_1_out ? ENWR : 1'bz;  // Controlled_Buffer controlled_buffer_3
  assign decoder_3_out0 = not_1_out ? ENWR : 1'bz;  // Controlled_Buffer controlled_buffer_4
  Zero_Eight_Register zero_eight_register_1 (
    .WD(WD), .CLK(Clk), .WR(WR[2:0]), .ENWR(decoder_3_out0), .R1_2(R1_2), .R1(R1[2:0]), .R2(R2[2:0]),
    .R2_2(R2_2), .ENR1(decoder_1_out0), .ENR2(decoder_2_out0));
  Normal_Eight_Register normal_eight_register_1 (
    .WD(WD), .CLK(Clk), .WR(WR[2:0]), .R1(R1[2:0]), .R2(R2[2:0]), .ENWR(decoder_3_out1),
    .ENR1(decoder_1_out1), .ENR2(decoder_2_out1), .R1_2(R1_2), .R2_2(R2_2));
  Normal_Eight_Register normal_eight_register_2 (
    .WD(WD), .CLK(Clk), .WR(WR[2:0]), .R1(R1[2:0]), .R2(R2[2:0]), .ENWR(decoder_3_out2),
    .ENR1(decoder_1_out2), .ENR2(decoder_2_out2), .R1_2(R1_2), .R2_2(R2_2));
  SP_Eight_Register sp_eight_register_1 (
    .WD(WD), .CLK(Clk), .WR(WR[2:0]), .ENWR(decoder_3_out3), .R1(R1[2:0]), .R2(R2[2:0]),
    .ENR1(decoder_1_out3), .ENR2(decoder_2_out3), .R1_2(R1_2), .R2_2(R2_2));
endmodule

// IM
module Instruction_Memory (
  input  [31:0] PC_DIR,
  output [31:0] INSTRUCTION
);

  wire [31:0] shifter_1_out;

  Shifter #(.width(32), .shift("lr")) shifter_1 (.in(PC_DIR), .\dist (5'b00010), .out(shifter_1_out));
  ROM #(.addrWidth(24), .dataWidth(32)) rom_1 (.addr(shifter_1_out[23:0]), .data(INSTRUCTION));  // open: sel
endmodule

// RWC
module Read_Write_Control (
  input  Read,
  input  Write,
  output Op
);

  wire not_1_out;

  not not_1 (not_1_out, Write);
  or or_1 (Op, not_1_out, Read);
endmodule

// DM
module Data_Memory (
  input  [31:0] ADDRESS_MEM,
  input  Clk,
  input  Read,
  input  Write,
  input  [31:0] WD,
  output [31:0] RD
);

  wire or_1_out, read_write_control_1_op;
  wire [31:0] shifter_1_out;

  Shifter #(.width(32), .shift("lr")) shifter_1 (.in(ADDRESS_MEM), .\dist (5'b00010), .out(shifter_1_out));
  or or_1 (or_1_out, Write, Read);
  Read_Write_Control read_write_control_1 (.Read(Read), .Op(read_write_control_1_op), .Write(Write));
  RAM #(.addrWidth(24), .dataWidth(32)) ram_1 (
    .addr(shifter_1_out[23:0]), .data(WD), .sel(or_1_out), .clk(Clk), .ld(read_write_control_1_op));  // open: clr

  assign RD = WD;
endmodule
