// Logisim project Unicycle Processor.circ as structural Verilog: 1 circuit, main circuit Processor
module Processor (
  input  in_1
);

  wire alu_thirty_two_bits_1_zero, ALUSRC, and_1_out, and_2_out, CLK, control_unit_1_enrbwr, JR, MEMREAD,
       MEMWRITE, not_1_out;
  wire [1:0] ALUOP, JUMPOPT, RDOPT, WDOPT;
  wire [2:0] ALU_OP;
  wire [3:0] adder_1_out;
  wire [4:0] RD;
  wire [25:0] ADDR;
  wire [27:0] adder_1_out_2, shifter_1_out;
  wire [31:0] adder_3_out, ALURESULT, controlled_buffer_1_out, DMDATA, INM, multiplexer_3_out,
       multiplexer_4_out, multiplexer_5_out, PC_8, PC_q, PCRESULT, register_bank_1_r1_2, shifter_2_out, WD,
       WDR;
  wire [31:26] INS;

  Clock clock_1 (.out(CLK));
  Register #(.width(32)) PC (.D(PCRESULT), .Q(PC_q), .clk(CLK), .clr(in_1));  // open: en
  // Probe on {INS, ADDR}
  // Probe on ADDR[25:21]
  // Probe on INS
  Adder #(.width(32)) adder_1 (.a(32'h4), .b(PC_q), .out({adder_1_out, adder_1_out_2}));  // open: cin, cout
  Instruction_Memory instruction_memory_1 (.PC_DIR(PC_q), .INSTRUCTION({INS, ADDR}));
  Adder #(.width(32)) adder_2 (.a(PC_q), .b(32'h8), .out(PC_8));  // open: cin, cout
  // Probe on ADDR[20:16]
  // Probe on ADDR
  // Probe on RD
  // Probe on ADDR[15:0]
  Shifter #(.width(28)) shifter_1 (.in({INS[27:26], ADDR}), .\dist (5'b00010), .out(shifter_1_out));
  Control_Unit control_unit_1 (
    .OP(INS), .RDOPT(RDOPT), .JUMPOPT(JUMPOPT), .MEMREAD(MEMREAD), .MEMWRITE(MEMWRITE), .WDPOPT(WDOPT),
    .ALUPOP(ALUOP), .ALUSRC(ALUSRC), .ENRBWR(control_unit_1_enrbwr));
  not not_1 (not_1_out, JR);
  // Probe on PCRESULT
  // Probe on RD
  and and_1 (and_1_out, control_unit_1_enrbwr, not_1_out);
  Multiplexer #(.select(2), .width(5)) multiplexer_1 (
    .in0(ADDR[20:16]), .in1(ADDR[15:11]), .in2({5{1'b1}}), .in3({5{1'b0}}), .out(RD), .sel(RDOPT));  // open: en
  Multiplexer #(.select(2), .width(32)) multiplexer_2 (
    .in0(ALURESULT), .in1(DMDATA), .in2(PC_8), .in3({32{1'b0}}), .out(WDR), .sel(WDOPT));  // open: en
  // Probe on ADDR[5:0]
  // Probe on ALURESULT
  // Probe on ALURESULT
  // Probe on PCRESULT
  Register_Bank register_bank_1 (
    .Clk(CLK), .R1(ADDR[25:21]), .R2(ADDR[20:16]), .WR(RD), .WD(WDR), .ENWR(and_1_out),
    .R1_2(register_bank_1_r1_2), .R2_2(WD));
  assign INM = {{16{ADDR[15]}}, ADDR[15:0]};  // Bit_Extender bit_extender_1
  // Probe on WDR
  Shifter #(.width(32)) shifter_2 (.in(INM), .\dist (5'b00010), .out(shifter_2_out));
  Multiplexer #(.width(32)) multiplexer_3 (.in0(WD), .in1(INM), .out(multiplexer_3_out), .sel(ALUSRC));  // open: en
  ALU_Controller alu_controller_1 (.ALU_Op(ALUOP), .FUNCT(ADDR[5:0]), .JR(JR), .ALU_OP_2(ALU_OP));
  Adder #(.width(32)) adder_3 (
    .a({adder_1_out, adder_1_out_2}), .b(shifter_2_out), .out(adder_3_out));  // open: cin, cout
  and and_2 (and_2_out, JUMPOPT[0], JUMPOPT[1], alu_thirty_two_bits_1_zero);
  ALU_Thirty_Two_Bits alu_thirty_two_bits_1 (
    .RESULT(ALURESULT), .ALU_CODE(ALU_OP), .R2(multiplexer_3_out), .CIN(1'b0), .R1(register_bank_1_r1_2),
    .ZERO(alu_thirty_two_bits_1_zero));
  // Probe on ALURESULT
  // Probe on PCRESULT
  // Probe on DMDATA
  // Probe on WD
  // Probe on PCRESULT
  Multiplexer #(.width(32)) multiplexer_4 (
    .in0({adder_1_out, adder_1_out_2}), .in1(register_bank_1_r1_2), .out(multiplexer_4_out), .sel(JR));  // open: en
  Multiplexer #(.width(32)) multiplexer_5 (
    .in0({adder_1_out, adder_1_out_2}), .in1(adder_3_out), .out(multiplexer_5_out), .sel(and_2_out));  // open: en
  // Data_Memory data_memory_1: pin names not known; wires that end beside it: ALURESULT, CLK, WD, MEMREAD, MEMWRITE, DMDATA
  assign controlled_buffer_1_out = MEMWRITE ? WD : 32'bz;  // Controlled_Buffer controlled_buffer_1
  Multiplexer #(.select(2), .width(32)) multiplexer_6 (
    .in0({adder_1_out, shifter_1_out}), .in1({adder_1_out, shifter_1_out}), .in2(multiplexer_4_out),
    .in3(multiplexer_5_out), .out(PCRESULT), .sel(JUMPOPT));  // open: en
  // Probe on controlled_buffer_1_out
  // Probe on WDR
  // Probe on WDR

  // Other names for the same wires on the sheet: FUNCT[5:0] = ADDR[5:0]; IMM[15:0] = ADDR[15:0]; INS[25:0] = ADDR;
  //   RT[4:0] = ADDR[20:16]; RS[4:0] = ADDR[25:21]; OPCODE[5:0] = INS

  // Notes on the sheet:
  //   j
  //   jal
  //   R
  //   lw
  //   sw
  //   beq
  //   Normal
  //   jr
endmodule
